# Fritzing sketch photon_dht11_sketch (saved by Fritzing 0.9.3b)
breadboards: 1

parts:
  Part1 = Photon
  DHT1 = DHT11 Humitidy and Temperature Sensor

nets:
  GND: Part1.GND, DHT1.GND
  3V3: Part1.3V3, DHT1.VDD

custom parts:
  DHT11 Humitidy and Temperature Sensor: DHT11 Humidity and Temperature Sensor
